# Fritzing sketch maintenance-panel (saved by Fritzing 0.9.3b)
breadboards: 1

parts:
  R1 = Resistor [tolerance=±5% resistance=220 package=THT]
  Part1 = Arduino Uno (Rev3)
  R2 = Resistor [tolerance=±5% resistance=220 package=THT]
  R3 = Resistor [tolerance=±5% resistance=220 package=THT]
  R4 = Resistor [tolerance=±5% resistance=220 package=THT]
  R5 = Resistor [tolerance=±5% resistance=220 package=THT]
  R6 = Resistor [tolerance=±5% resistance=220 package=THT]
  S1 = Pushbutton [package="[THT]"]
  R7 = Resistor [tolerance=±5% resistance=220 package=THT]
  L1 = Solenoid

nets:
  N1: R1.Pin_0, R2.Pin_1, R3.Pin_1, R7.Pin_0
  N2: R1.Pin_1, Part1.D9_PWM, R4.Pin_1
  N3: Part1.D8, R2.Pin_0, R5.Pin_1
  N4: Part1.D10_PWM/SS, R6.Pin_0
  N5: Part1.D11_PWM/MOSI, R5.Pin_0
  N6: Part1.D12/MISO, R4.Pin_0
  N7: Part1.D13/SCK, S1.Pin_1, S1.Pin_2, R7.Pin_1
  N8: Part1.D6_PWM, L1.pin2
  N9: Part1.D7, R3.Pin_0, R6.Pin_1
  N10: S1.Pin_3, S1.Pin_4
